// Logisim project ALU.circ as structural Verilog: 1 circuit, main circuit main
module main (
  input  CARRY_IN,
  input  BORROW_IN,
  input  [15:0] A_IN,
  input  [15:0] B_IN,
  input  ADD,
  input  SUB,
  input  NOT_A,
  input  A_AND_B,
  input  A_OR_B,
  input  A_XOR_B,
  input  A_NAND_B,
  input  A_NOR_B,
  output CARRY_OUT,
  output BORROW_OUT,
  output GREATER,
  output EQUAL,
  output LESS,
  output [15:0] DATA_OUT,
  output ZERO_FLAG
);

  wire and_2_out, and_3_out, and_4_out, and_5_out, and_6_out, and_7_out, and_8_out, and_9_out, and_10_out,
       and_11_out, and_12_out, and_13_out, and_14_out, and_15_out, not_2_out, not_3_out, not_4_out,
       not_5_out, not_6_out, not_7_out, not_8_out, not_9_out, not_10_out, not_11_out, not_12_out, not_13_out,
       not_14_out, not_15_out, not_16_out, not_17_out;
  wire [15:0] adder_1_out, and_1_out, nand_1_out, nor_1_out, not_1_out, or_1_out, or_2_out, subtractor_1_out,
       xor_1_out;

  assign DATA_OUT = ADD ? adder_1_out : 16'bz;  // Controlled_Buffer controlled_buffer_1
  Adder #(.width(16)) adder_1 (.a(A_IN), .b(B_IN), .out(adder_1_out), .cin(CARRY_IN), .cout(CARRY_OUT));
  assign DATA_OUT = SUB ? subtractor_1_out : 16'bz;  // Controlled_Buffer controlled_buffer_2
  Subtractor #(.width(16)) subtractor_1 (
    .a(A_IN), .b(B_IN), .out(subtractor_1_out), .bin(BORROW_IN), .bout(BORROW_OUT));
  Comparator #(.width(16)) comparator_1 (.a(A_IN), .b(B_IN), .gt(GREATER), .eq(EQUAL), .lt(LESS));
  assign not_1_out = ~A_IN;  // NOT_Gate not_1, 16 bits wide
  assign DATA_OUT = NOT_A ? not_1_out : 16'bz;  // Controlled_Buffer controlled_buffer_3
  assign and_1_out = A_IN & B_IN;  // AND_Gate and_1, 16 bits wide
  assign DATA_OUT = A_AND_B ? and_1_out : 16'bz;  // Controlled_Buffer controlled_buffer_4
  assign or_1_out = A_IN | B_IN;  // OR_Gate or_1, 16 bits wide
  assign DATA_OUT = A_OR_B ? or_1_out : 16'bz;  // Controlled_Buffer controlled_buffer_5
  assign xor_1_out = A_IN ^ B_IN;  // XOR_Gate xor_1, 16 bits wide
  assign DATA_OUT = A_XOR_B ? xor_1_out : 16'bz;  // Controlled_Buffer controlled_buffer_6
  assign nand_1_out = ~(A_IN & B_IN);  // NAND_Gate nand_1, 16 bits wide
  assign DATA_OUT = A_NAND_B ? nand_1_out : 16'bz;  // Controlled_Buffer controlled_buffer_7
  assign nor_1_out = ~(A_IN | B_IN);  // NOR_Gate nor_1, 16 bits wide
  assign DATA_OUT = A_NOR_B ? nor_1_out : 16'bz;  // Controlled_Buffer controlled_buffer_8
  assign or_2_out = DATA_OUT;  // OR_Gate or_2, 16 bits wide OR_Gate
  not not_2 (not_2_out, or_2_out[0]);
  not not_3 (not_3_out, or_2_out[1]);
  not not_4 (not_4_out, or_2_out[2]);
  not not_5 (not_5_out, or_2_out[3]);
  not not_6 (not_6_out, or_2_out[4]);
  not not_7 (not_7_out, or_2_out[5]);
  and and_2 (and_2_out, not_2_out, not_3_out);
  and and_3 (and_3_out, and_2_out, not_4_out);
  and and_4 (and_4_out, and_3_out, not_5_out);
  and and_5 (and_5_out, and_4_out, not_6_out);
  and and_6 (and_6_out, and_5_out, not_7_out);
  and and_7 (and_7_out, and_6_out, not_8_out);
  not not_8 (not_8_out, or_2_out[6]);
  not not_9 (not_9_out, or_2_out[7]);
  not not_10 (not_10_out, or_2_out[8]);
  not not_11 (not_11_out, or_2_out[9]);
  not not_12 (not_12_out, or_2_out[10]);
  not not_13 (not_13_out, or_2_out[11]);
  not not_14 (not_14_out, or_2_out[12]);
  not not_15 (not_15_out, or_2_out[13]);
  and and_8 (and_8_out, and_7_out, not_9_out);
  and and_9 (and_9_out, and_8_out, not_10_out);
  and and_10 (and_10_out, and_9_out, not_11_out);
  and and_11 (and_11_out, and_10_out, not_12_out);
  and and_12 (and_12_out, and_11_out, not_13_out);
  and and_13 (and_13_out, and_12_out, not_14_out);
  and and_14 (and_14_out, and_13_out, not_15_out);
  and and_15 (and_15_out, and_14_out, not_16_out);
  Pull_Resistor pull_resistor_1 (.node(or_2_out[0]));
  Pull_Resistor pull_resistor_2 (.node(or_2_out[1]));
  Pull_Resistor pull_resistor_3 (.node(or_2_out[2]));
  Pull_Resistor pull_resistor_4 (.node(or_2_out[3]));
  Pull_Resistor pull_resistor_5 (.node(or_2_out[4]));
  Pull_Resistor pull_resistor_6 (.node(or_2_out[5]));
  Pull_Resistor pull_resistor_7 (.node(or_2_out[6]));
  Pull_Resistor pull_resistor_8 (.node(or_2_out[7]));
  Pull_Resistor pull_resistor_9 (.node(or_2_out[8]));
  Pull_Resistor pull_resistor_10 (.node(or_2_out[9]));
  Pull_Resistor pull_resistor_11 (.node(or_2_out[10]));
  Pull_Resistor pull_resistor_12 (.node(or_2_out[11]));
  Pull_Resistor pull_resistor_13 (.node(or_2_out[12]));
  Pull_Resistor pull_resistor_14 (.node(or_2_out[13]));
  Pull_Resistor pull_resistor_15 (.node(or_2_out[14]));
  Pull_Resistor pull_resistor_16 (.node(or_2_out[15]));
  not not_16 (not_16_out, or_2_out[14]);
  not not_17 (not_17_out, or_2_out[15]);
  and and_16 (ZERO_FLAG, and_15_out, not_17_out);
endmodule
