// Logisim project fourBitALU.circ as structural Verilog: 1 circuit, main circuit main
module main (
  input  [3:0] A,
  input  [3:0] B,
  input  [2:0] selectLines,
  input  enable,
  output [3:0] D
);

  // Adder #(.width(4)) adder_1: pin names not known; wires that end beside it: A, B, 4'b0000, A
  // Subtractor #(.width(4)) subtractor_1: pin names not known; wires that end beside it: A, B, 4'b0000, B
  // Subtractor #(.width(4)) subtractor_2: pin names not known; wires that end beside it: B, A, 4'b0000, B
  Negator #(.width(4)) negator_1 (.in(A), .out(A));
  Negator #(.width(4)) negator_2 (.in(B), .out(B));
  Multiplexer #(.enable("true"), .select(3), .width(4)) multiplexer_1 (
    .in0(A), .in1(B), .in2(A), .in3(B), .in4(B), .in5(A), .in6(B), .in7(4'b0000), .out(D));  // open: sel, en
endmodule
