// Logisim project fourBitShifter.circ as structural Verilog: 1 circuit, main circuit main
module main (
  input  in_1,
  input  [3:0] A,
  input  enable,
  input  [3:0] selectLines,
  output [3:0] D,
  output A3,
  output A0
);

  wire multiplexer_1_out;

  Multiplexer #(.enable("true"), .select(3)) multiplexer_1 (
    .in0(in_1), .in1(in_1), .in2(A[3]), .in3(in_1), .in4(A[3]), .in5(A[0]), .in6(in_1), .in7(in_1),
    .out(multiplexer_1_out), .sel(selectLines[2:0]), .en(enable));
  Multiplexer #(.enable("true")) multiplexer_2 (
    .in0(multiplexer_1_out), .in1(A[1]), .out(D[0]), .sel(selectLines[3]), .en(enable));
  Multiplexer #(.enable("true")) multiplexer_3 (.in0(A[0]), .in1(A[2]), .out(D[1]), .sel(selectLines[3]), .en(enable));
  Multiplexer #(.enable("true")) multiplexer_4 (.in0(A[1]), .in1(A[3]), .out(D[2]), .sel(selectLines[3]), .en(enable));
  Multiplexer #(.enable("true")) multiplexer_5 (
    .in0(A[2]), .in1(multiplexer_1_out), .out(D[3]), .sel(selectLines[3]), .en(enable));

  assign A0 = A[0];
  assign A3 = A[3];
endmodule
